// Logisim project Lab01_Kiyazov_Mux21.circ as structural Verilog: 1 circuit, main circuit main
module main (
  input  Sel,
  input  In1,
  input  In2,
  output out_4
);

  wire and_1_out, and_2_out, not_1_out;

  not not_1 (not_1_out, Sel);
  and and_1 (and_1_out, In1, not_1_out);
  and and_2 (and_2_out, Sel, In2);
  or or_1 (out_4, and_1_out, and_2_out);

  // Notes on the sheet:
  //   10 Feb 2025
  //   Lab01_Kiyazov_Aziret-Sultan_Mux2to1
endmodule
