// Logisim project Lab02_Bool.circ as structural Verilog: 3 circuits, main circuit main
module main (
  input  A1,
  input  B1,
  input  C1,
  input  A2,
  input  B2,
  input  C2,
  input  D2,
  output True1,
  output True2
);

  Equation_1 equation_1_1 (.A1(A1), .B1(B1), .C1(C1), .OUT1(True1));
  Equation_2 equation_2_1 (.A2(A2), .B2(B2), .C2(C2), .D2(D2), .OUT2(True2));

  // Notes on the sheet:
  //   10 Feb 2024
  //   Lab02 Kiyazov Aziret-Sultan
endmodule

module Equation_2 (
  input  A2,
  input  B2,
  input  C2,
  input  D2,
  output OUT2
);

  wire and_1_out, and_2_out, and_3_out, and_4_out;

  and and_1 (and_1_out, ~A2, ~B2, C2, ~D2);  // AND_Gate
  and and_2 (and_2_out, ~A2, B2, C2, D2);  // AND_Gate
  and and_3 (and_3_out, A2, ~B2, C2, ~D2);  // AND_Gate
  and and_4 (and_4_out, A2, B2, C2, ~D2);  // AND_Gate
  or or_1 (OUT2, and_1_out, and_2_out, and_3_out, and_4_out);
endmodule

module Equation_1 (
  input  A1,
  input  B1,
  input  C1,
  output OUT1
);

  wire and_1_out, and_2_out, and_3_out;

  and and_1 (and_1_out, ~A1, B1, ~C1);  // AND_Gate
  and and_2 (and_2_out, A1, ~B1, ~C1);  // AND_Gate
  and and_3 (and_3_out, A1, B1, C1);
  or or_1 (OUT1, and_1_out, and_2_out, and_3_out);
endmodule
