// Logisim project 1BitAdder.circ as structural Verilog
module Half_Adder (
  input  InA,
  input  InB,
  output Out_Sum,
  output Out_Carry
);

  wire and_1_out, and_2_out, not_1_out, not_2_out;

  not not_1 (not_1_out, InA);
  not not_2 (not_2_out, InB);
  and and_1 (and_1_out, not_1_out, InB);
  and and_2 (and_2_out, InA, not_2_out);
  and and_3 (Out_Carry, InA, InB);
  or or_1 (Out_Sum, and_1_out, and_2_out);

  // Notes on the sheet:
  //   1 Bit Adder. Kiyazov Aziret
  //   11 Feb 2025
endmodule
