// Logisim project Universal.circ as structural Verilog: 7 circuits, main circuit Universal
module Universal (
  input  Clock_Universal,
  input  Reset_Universal,
  input  [2:0] Sel,
  output [3:0] OutUniversal
);

  wire [3:0] decadecounter_1_counter_decade, downcounter_1_counter_down, johnsoncounter_1_jhonson_counter,
       ringcounter_1_ring, upcounter_1_counter_up;

  UpCounter upcounter_1 (.Clock(Clock_Universal), .Reset(Reset_Universal), .Counter_Up(upcounter_1_counter_up));
  DownCounter downcounter_1 (
    .Clock1(Clock_Universal), .Reset1(Reset_Universal), .Counter_Down(downcounter_1_counter_down));
  DecadeCounter decadecounter_1 (
    .Clock2(Clock_Universal), .Reset2(Reset_Universal), .Counter_Decade(decadecounter_1_counter_decade));
  RingCounter ringcounter_1 (.Clock3(Clock_Universal), .Reset3(Reset_Universal), .Ring(ringcounter_1_ring));
  JohnsonCounter johnsoncounter_1 (
    .Clock4(Clock_Universal), .Reset4(Reset_Universal), .Jhonson_Counter(johnsoncounter_1_jhonson_counter));
  Multiplexer #(.select(3), .width(4)) multiplexer_1 (
    .in0(upcounter_1_counter_up), .in1(downcounter_1_counter_down), .in2(decadecounter_1_counter_decade),
    .in3(ringcounter_1_ring), .in4(johnsoncounter_1_jhonson_counter), .out(OutUniversal), .sel(Sel));  // open: in5, in6, in7
endmodule

module main (
  input  Reset,
  input  Reset_Un,
  input  [2:0] SelectUn
);

  wire clk_out;
  wire [3:0] universal_1_outuniversal, upcounter_1_counter_up;

  Clock clk (.out(clk_out));
  Clock #(.highDuration(4), .lowDuration(4)) sysclk ();  // open: out
  UpCounter upcounter_1 (.Clock(clk_out), .Reset(Reset), .Counter_Up(upcounter_1_counter_up));
  // Probe on upcounter_1_counter_up
  Universal universal_1 (
    .Clock_Universal(clk_out), .Reset_Universal(Reset_Un), .Sel(SelectUn),
    .OutUniversal(universal_1_outuniversal));
  Hex_Digit_Display hex_digit_display_1 (.value(upcounter_1_counter_up));  // open: dp
  // Probe on universal_1_outuniversal
  Hex_Digit_Display hex_digit_display_2 (.value(universal_1_outuniversal));  // open: dp
endmodule

module UpCounter (
  input  Clock,
  input  Reset,
  output [3:0] Counter_Up
);

  wire d_ff_1_qn, d_ff_2_qn, d_ff_3_qn, d_ff_4_qn;

  D_Flip_Flop d_ff_1 (.D(d_ff_1_qn), .clk(Clock), .Q(Counter_Up[0]), .Qn(d_ff_1_qn), .reset(Reset));  // open: preset
  D_Flip_Flop d_ff_2 (
    .D(d_ff_2_qn), .clk(d_ff_1_qn), .Q(Counter_Up[1]), .Qn(d_ff_2_qn), .reset(Reset));  // open: preset
  D_Flip_Flop d_ff_3 (
    .D(d_ff_3_qn), .clk(d_ff_2_qn), .Q(Counter_Up[2]), .Qn(d_ff_3_qn), .reset(Reset));  // open: preset
  D_Flip_Flop d_ff_4 (
    .D(d_ff_4_qn), .clk(d_ff_3_qn), .Q(Counter_Up[3]), .Qn(d_ff_4_qn), .reset(Reset));  // open: preset
endmodule

module DownCounter (
  input  Clock1,
  input  Reset1,
  output [3:0] Counter_Down
);

  wire d_ff_1_qn, d_ff_2_qn, d_ff_3_qn, d_ff_4_qn;

  D_Flip_Flop d_ff_1 (
    .D(d_ff_1_qn), .clk(Clock1), .Q(Counter_Down[0]), .Qn(d_ff_1_qn), .preset(Reset1));  // open: reset
  D_Flip_Flop d_ff_2 (
    .D(d_ff_2_qn), .clk(Counter_Down[0]), .Q(Counter_Down[1]), .Qn(d_ff_2_qn), .preset(Reset1));  // open: reset
  D_Flip_Flop d_ff_3 (
    .D(d_ff_3_qn), .clk(Counter_Down[1]), .Q(Counter_Down[2]), .Qn(d_ff_3_qn), .preset(Reset1));  // open: reset
  D_Flip_Flop d_ff_4 (
    .D(d_ff_4_qn), .clk(Counter_Down[2]), .Q(Counter_Down[3]), .Qn(d_ff_4_qn), .preset(Reset1));  // open: reset
endmodule

module DecadeCounter (
  input  Clock2,
  input  Reset2,
  output [3:0] Counter_Decade
);

  wire and_1_out, d_ff_1_qn, d_ff_2_qn, d_ff_3_qn, d_ff_4_qn, or_1_out;

  D_Flip_Flop d_ff_1 (
    .D(d_ff_1_qn), .clk(Clock2), .Q(Counter_Decade[0]), .Qn(d_ff_1_qn), .reset(or_1_out));  // open: preset
  or or_1 (or_1_out, Reset2, and_1_out);
  D_Flip_Flop d_ff_2 (
    .D(d_ff_2_qn), .clk(d_ff_1_qn), .Q(Counter_Decade[1]), .Qn(d_ff_2_qn), .reset(or_1_out));  // open: preset
  D_Flip_Flop d_ff_3 (
    .D(d_ff_3_qn), .clk(d_ff_2_qn), .Q(Counter_Decade[2]), .Qn(d_ff_3_qn), .reset(or_1_out));  // open: preset
  D_Flip_Flop d_ff_4 (
    .D(d_ff_4_qn), .clk(d_ff_3_qn), .Q(Counter_Decade[3]), .Qn(d_ff_4_qn), .reset(or_1_out));  // open: preset
  and and_1 (and_1_out, Counter_Decade[1], Counter_Decade[3]);
endmodule

module RingCounter (
  input  Clock3,
  input  Reset3,
  output [3:0] Ring
);

  D_Flip_Flop d_ff_1 (.D(Ring[3]), .clk(Clock3), .Q(Ring[0]), .preset(Reset3));  // open: Qn, reset
  D_Flip_Flop d_ff_2 (.D(Ring[0]), .clk(Clock3), .Q(Ring[1]), .reset(Reset3));  // open: Qn, preset
  D_Flip_Flop d_ff_3 (.D(Ring[1]), .clk(Clock3), .Q(Ring[2]), .reset(Reset3));  // open: Qn, preset
  D_Flip_Flop d_ff_4 (.D(Ring[2]), .clk(Clock3), .Q(Ring[3]), .reset(Reset3));  // open: Qn, preset
endmodule

module JohnsonCounter (
  input  Clock4,
  input  Reset4,
  output [3:0] Jhonson_Counter
);

  wire d_ff_4_qn;

  D_Flip_Flop d_ff_1 (.D(d_ff_4_qn), .clk(Clock4), .Q(Jhonson_Counter[0]), .preset(Reset4));  // open: Qn, reset
  D_Flip_Flop d_ff_2 (
    .D(Jhonson_Counter[0]), .clk(Clock4), .Q(Jhonson_Counter[1]), .reset(Reset4));  // open: Qn, preset
  D_Flip_Flop d_ff_3 (
    .D(Jhonson_Counter[1]), .clk(Clock4), .Q(Jhonson_Counter[2]), .reset(Reset4));  // open: Qn, preset
  D_Flip_Flop d_ff_4 (
    .D(Jhonson_Counter[2]), .clk(Clock4), .Q(Jhonson_Counter[3]), .Qn(d_ff_4_qn), .reset(Reset4));  // open: preset
endmodule
